// Logisim project Harvard-8Bit-CPU.circ as structural Verilog: 2 circuits, main circuit LIA -> 0x01 -> Load A register immidiate.
module LIA____0x01____Load_A_register_immidiate (
  output [7:0] ADDR_IMM,
  output [7:0] DATA,
  output [7:0] OUT,
  output [3:0] FLAGS
);

  wire A_IN, A_OUT, ALU_0, ALU_1, ALU_2, B_IN, B_OUT, CLK, clock_1_out, FLAGS_IN, HALT, IMM, IR_IN, MAR_IN,
       nCLK, not_1_out, OUT_IN, PC_IN, PC_INC, PC_OUT, RAM_IN, RAM_OUT, ROM_OUT, SEQ_CLR;
  wire [2:0] counter_2_q;
  wire [3:0] alu_1_zero;
  wire [7:0] A, alu_1_output, B, counter_1_q, IR_q, MAR_q, multiplexer_1_out;
  wire [15:0] rom_2_data;
  wire [15:8] controlled_buffer_2_out;
  wire [15:13] rom_1_data;

  Register MAR (.D(ADDR_IMM), .en(MAR_IN), .Q(MAR_q), .clk(CLK));  // open: clr
  Counter counter_1 (.load(PC_IN), .D(ADDR_IMM), .count(PC_INC), .Q(counter_1_q), .clk(CLK));  // open: carry, clr
  Counter #(.width(3), .max('h7)) counter_2 (
    .count(nCLK), .Q(counter_2_q), .clk(nCLK), .clr(SEQ_CLR));  // open: load, D, carry
  Clock clock_1 (.out(clock_1_out));
  not not_1 (not_1_out, HALT);
  assign ADDR_IMM = PC_OUT ? counter_1_q : 8'bz;  // Controlled_Buffer controlled_buffer_1
  and and_1 (CLK, clock_1_out, not_1_out);
  ROM #(.addrWidth(16), .dataWidth(16)) rom_1 (
    .addr({counter_2_q, IR_q, FLAGS, 1'b0}),
    .data({rom_1_data, OUT_IN, SEQ_CLR, IMM, ALU_2, ALU_1, ALU_0, B_IN, A_IN, ROM_OUT, MAR_IN, IR_IN, PC_OUT, RAM_IN}),
    .sel(1'b1));
  not not_2 (nCLK, CLK);
  assign {controlled_buffer_2_out, ADDR_IMM} = ROM_OUT ? rom_2_data : 16'bz;  // Controlled_Buffer controlled_buffer_2
  ROM #(.addrWidth(16), .dataWidth(16)) rom_2 (.addr({{8{1'b0}}, MAR_q}), .data(rom_2_data), .sel(1'b1));
  Register IR (.D(controlled_buffer_2_out), .en(IR_IN), .Q(IR_q), .clk(CLK));  // open: clr
  Multiplexer #(.width(8)) multiplexer_1 (.in0(DATA), .in1(ADDR_IMM), .out(multiplexer_1_out), .sel(IMM));  // open: en
  Register u_A (.D(multiplexer_1_out), .en(A_IN), .Q(A), .clk(CLK));  // open: clr
  Register u_B (.D(multiplexer_1_out), .en(B_IN), .Q(B), .clk(CLK));  // open: clr
  RAM #(.bus("separate")) ram_1 (
    .addr(MAR_q), .din(DATA), .data(DATA), .str(RAM_IN), .sel(1'b1), .clk(CLK), .ld(RAM_OUT));  // open: clr
  assign DATA = A_OUT ? A : 8'bz;  // Controlled_Buffer controlled_buffer_3
  assign DATA = B_OUT ? B : 8'bz;  // Controlled_Buffer controlled_buffer_4
  Register u_OUT (.D(DATA), .en(OUT_IN), .Q(OUT), .clk(CLK));  // open: clr
  Decoder #(.select(3)) decoder_1 (
    .out1(HALT), .out2(PC_INC), .out3(PC_IN), .out4(RAM_OUT), .out5(A_OUT), .out6(B_OUT), .out7(FLAGS_IN),
    .sel({rom_1_data[13], rom_1_data[14], rom_1_data[15]}), .en(1'b1));  // open: out0
  Register #(.width(4)) u_FLAGS (.D(alu_1_zero), .en(FLAGS_IN), .Q(FLAGS), .clk(CLK));  // open: clr
  assign DATA = FLAGS_IN ? alu_1_output : 8'bz;  // Controlled_Buffer controlled_buffer_5
  ALU u_alu_1 (
    .A(A), .Select({ALU_2, ALU_1, ALU_0}), .B(B), .Carry_Out(alu_1_zero[3]), .Output(alu_1_output),
    .Zero(alu_1_zero[0]), .Overflow(alu_1_zero[1]), .Negative(alu_1_zero[2]));

  // Other names for the same wires on the sheet: CNVZ[3:0] = FLAGS; IMM_VAL[7:0] = ADDR_IMM

  // Notes on the sheet:
  //   PC
  //   SEQ
  //   INST
  //   CONTROL ROM
  //   CLOCK
  //   PROGRAM ROM
  //   ADDR/IMM
  //   contents of rom_1 (hex, n*v repeats v):
  //   a 0 a 0 a 0 a 0 a 0 a 0 a 0 a 0 a 0 a 0 a 0 a 0 a 0 a 0 a 0 a 0 a 0 a 0 a 0 a 0 a 0 a 0 a 0 a 0 a 0
  //   a 0 a 0 a 0 a 0 a 0 a 0 a 0 a 0 a 0 a 0 a 0 a 0 a 0 a 0 a 0 a 0 a 0 a 0 a 0 a 0 a 0 a 0 a 0 8000 0
  //   8000 0 8000 0 8000 0 8000 0 8000 0 8000 0 8000 0 8000 0 8000 0 8000 0 8000 0 8000 0 8000 0 8000 0
  //   8000 0 a 0 a 0 a 0 a 0 a 0 a 0 a 0 a 0 a 0 a 0 a 0 a 0 a 0 a 0 a 0 a 0 a 0 a 0 a 0 a 0 a 0 a 0 a 0 a
  //   0 a 0 a 0 a 0 a 0 a 0 a 0 a 0 a 0 a 0 a 0 a 0 a 0 a 0 a 0 a 0 a 0 a 0 a 0 a 0 a 0 a 0 a 0 a 0 a 0 a
  //   0 a 0 a 0 a 0 a 0 a 0 a 0 a 0 a 0 a 0 a 0 a 0 a 0 a 0 a 0 a 0 a 0 a 0 a 0 a 0 a 0 a 0 a 0 a 0 a 0 a
  //   0 a 0 a 0 a 0 a 0 a 0 a 0 a 0 a 0 a 0 a 0 a 0 a 0 a 0 a 0 a 0 a 0 a 0 a 0 a 0 a 0 a 0 a 0 c018 0
  //   c018 0 c018 0 c018 0 c018 0 c018 0 c018 0 c018 0 c018 0 c018 0 c018 0 c018 0 c018 0 c018 0 c018 0
  //   c018 0 a 0 a 0 a 0 a 0 a 0 a 0 a 0 a 0 a 0 a 0 a 0 a 0 a 0 a 0 a 0 a 97*0 a 0 a 0 a 0 a 0 a 0 a 0 a
  //   0 a 0 a 0 a 0 a 0 a 0 a 0 a 0 a 0 a 0 a 0 a 0 a 0 a 0 a 0 a 0 a 0 a 0 a 0 a 0 a 0 a 0 a 0 a 0 a 0 a
  //   0 a 0 c018 0 a 0 c018 0 a 0 c018 0 a 0 c018 0 a 0 c018 0 a 0 c018 0 a 0 c018 0 a 0 c018 0 a 0 a 0
  //   c018 0 c018 0 a 0 a 0 c018 0 c018 0 a 0 a 0 c018 0 c018 0 a 0 a 0 c018 0 c018 0 a 0 a 0 a 0 a 0 c018
  //   0 c018 0 c018 0 c018 0 a 0 a 0 a 0 a 0 c018 0 c018 0 c018 0 c018 0 a 0 a 0 a 0 a 0 a 0 a 0 a 0 a 0
  //   c018 0 c018 0 c018 0 c018 0 c018 0 c018 0 c018 0 c018 0 a 0 a 0 a 0 a 0 a 0 a 0 a 0 a 0 a 0 a 0 a 0
  //   a 0 a 0 a 0 a 0 a 0 a 0 a 0 a 0 a 0 a 0 a 0 a 0 a 0 a 0 a 0 a 0 a 0 a 0 a 0 a 0 a 0 a 0 a 0 a 0 a 0
  //   a 0 a 0 a 0 a 0 a 0 a 0 a 0 a 0 a 0 a 0 a 0 a 0 a 0 a 0 a 0 a 0 a 0 a 0 a 0 a 0 a 0 a 0 a 0 a 0 a 0
  //   a 0 a 0 a 7393*0 4014 0 4014 0 4014 0 4014 0 4014 0 4014 0 4014 0 4014 0 4014 0 4014 0 4014 0 4014 0
  //   4014 0 4014 0 4014 0 4014 0 4014 0 4014 0 4014 0 4014 0 4014 0 4014 0 4014 0 4014 0 4014 0 4014 0
  //   4014 0 4014 0 4014 0 4014 0 4014 0 4014 0 4014 0 4014 0 4014 0 4014 0 4014 0 4014 0 4014 0 4014 0
  //   4014 0 4014 0 4014 0 4014 0 4014 0 4014 0 4014 0 4014 33*0 4014 0 4014 0 4014 0 4014 0 4014 0 4014 0
  //   4014 0 4014 0 4014 0 4014 0 4014 0 4014 0 4014 0 4014 0 4014 0 4014 0 4014 0 4014 0 4014 0 4014 0
  //   4014 0 4014 0 4014 0 4014 0 4014 0 4014 0 4014 0 4014 0 4014 0 4014 0 4014 0 4014 0 4014 0 4014 0
  //   4014 0 4014 0 4014 0 4014 0 4014 0 4014 0 4014 0 4014 0 4014 0 4014 0 4014 0 4014 0 4014 0 4014 0
  //   4014 0 4014 0 4014 0 4014 0 4014 0 4014 0 4014 0 4014 0 4014 0 4014 0 4014 0 4014 0 4014 0 4014 0
  //   4014 0 4014 0 4014 0 4014 0 4014 0 4014 0 4014 0 4014 0 4014 0 4014 0 4014 0 4014 0 4014 0 4014 0
  //   4014 0 4014 0 4014 0 4014 0 4014 0 4014 0 4014 0 4014 0 4014 0 4014 0 4014 0 4014 0 4014 0 4014 0
  //   4014 0 4014 0 4014 0 4014 0 4014 0 4014 0 4014 0 4014 0 4014 0 4014 0 4014 0 4014 0 4014 0 4014 0
  //   4014 0 4014 0 4014 0 4014 0 4014 0 4014 0 4014 0 4014 0 4014 0 4014 0 4014 0 4014 0 4014 0 4014 0
  //   4014 0 4014 0 4014 0 4014 0 4014 0 4014 0 4014 0 4014 0 4014 0 4014 97*0 4014 0 4014 0 4014 0 4014 0
  //   4014 0 4014 0 4014 0 4014 0 4014 0 4014 0 4014 0 4014 0 4014 0 4014 0 4014 0 4014 0 4014 0 4014 0
  //   4014 0 4014 0 4014 0 4014 0 4014 0 4014 0 4014 0 4014 0 4014 0 4014 0 4014 0 4014 0 4014 0 4014 0
  //   4014 0 4014 0 4014 0 4014 0 4014 0 4014 0 4014 0 4014 0 4014 0 4014 0 4014 0 4014 0 4014 0 4014 0
  //   4014 0 4014 0 4014 0 4014 0 4014 0 4014 0 4014 0 4014 0 4014 0 4014 0 4014 0 4014 0 4014 0 4014 0
  //   4014 0 4014 0 4014 0 4014 0 4014 0 4014 0 4014 0 4014 0 4014 0 4014 0 4014 0 4014 0 4014 0 4014 0
  //   4014 0 4014 0 4014 0 4014 0 4014 0 4014 0 4014 0 4014 0 4014 0 4014 0 4014 0 4014 0 4014 0 4014 0
  //   4014 0 4014 0 4014 0 4014 0 4014 0 4014 0 4014 0 4014 0 4014 0 4014 0 4014 0 4014 0 4014 0 4014 0
  //   4014 0 4014 0 4014 0 4014 0 4014 0 4014 0 4014 0 4014 0 4014 0 4014 0 4014 0 4014 0 4014 0 4014 0
  //   4014 0 4014 0 4014 0 4014 0 4014 0 4014 0 4014 0 4014 0 4014 0 4014 0 4014 0 4014 0 4014 0 4014 0
  //   4014 0 4014 0 4014 0 4014 0 4014 0 4014 0 4014 0 4014 0 4014 0 4014 0 4014 0 4014 0 4014 0 4014 0
  //   4014 0 4014 0 4014 0 4014 0 4014 0 4014 0 4014 0 4014 0 4014 0 4014 0 4014 0 4014 0 4014 0 4014 0
  //   4014 0 4014 7393*0 800 0 800 0 800 0 800 0 800 0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
  //   contents of rom_2 (hex, n*v repeats v):
  //   101 501 200 600 b00 1500 800 b00 1500 900 1200 a04
  //   RAM
  //   DATA
endmodule

module ALU (
  input  [7:0] A,
  input  [2:0] Select,
  input  [7:0] B,
  output [7:0] Output,
  output Zero,
  output Carry_Out,
  output Overflow,
  output Negative
);

  wire adder_1_cout, controlled_buffer_1_out, decoder_1_out1, decoder_1_out2, or_1_out;
  wire [6:0] adder_1_out;
  wire [7:0] AND, bit_extender_1_out, bit_extender_2_out, OR, XOR, xor_1_out, xor_2_out;

  Decoder #(.select(3)) decoder_1 (
    .out1(decoder_1_out1), .out2(decoder_1_out2), .sel(Select), .en(1'b1));  // open: out0, out3, out4, out5, out6, out7
  assign controlled_buffer_1_out = decoder_1_out2 ? decoder_1_out2 : 1'bz;  // Controlled_Buffer controlled_buffer_1
  assign controlled_buffer_1_out = decoder_1_out1 ? decoder_1_out1 : 1'bz;  // Controlled_Buffer controlled_buffer_2
  assign bit_extender_1_out = {{7{decoder_1_out1}}, decoder_1_out1};  // Bit_Extender bit_extender_1
  assign bit_extender_2_out = {{7{decoder_1_out2}}, decoder_1_out2};  // Bit_Extender bit_extender_2
  assign xor_1_out = bit_extender_1_out ^ A;  // XOR_Gate xor_1, 8 bits wide
  assign xor_2_out = bit_extender_2_out ^ B;  // XOR_Gate xor_2, 8 bits wide
  Adder #(.width(7)) adder_1 (
    .a(xor_1_out[6:0]), .b(xor_2_out[6:0]), .out(adder_1_out), .cin(controlled_buffer_1_out),
    .cout(adder_1_cout));
  Adder #(.width(1)) adder_2 (.a(xor_1_out[7]), .b(xor_2_out[7]), .out(Negative), .cin(adder_1_cout), .cout(Carry_Out));
  Multiplexer #(.select(3), .width(8)) multiplexer_1 (
    .in0({8{1'b0}}), .in1({Negative, adder_1_out}), .in2({Negative, adder_1_out}),
    .in3({Negative, adder_1_out}), .in4(XOR), .in5(AND), .in6(OR), .in7({8{1'b1}}), .out(Output), .sel(Select));  // open: en
  xor xor_3 (Overflow, adder_1_cout, Carry_Out);
  not not_1 (Zero, or_1_out);
  or or_1 (or_1_out, Output[0], Output[1], Output[2], Output[3], Output[4], Output[5], Output[6], Output[7]);
  assign XOR = A ^ B;  // XOR_Gate xor_4, 8 bits wide
  assign OR = A | B;  // OR_Gate or_2, 8 bits wide
  assign AND = A & B;  // AND_Gate and_1, 8 bits wide

  // Notes on the sheet:
  //   000 -> CLEAR
  //   001 -> B - A
  //   010 -> A - B
  //   011 -> A PLUS B
  //   100 -> A XOR B
  //   101 -> AB
  //   110 -> A + B
  //   111 -> PRESET
endmodule
